# Fritzing sketch fritzing_schematic (saved by Fritzing 0.9.10b)
breadboards: 1

parts:
  Part1 = Arduino Uno (Rev3)
  R1 = Resistor [tolerance=±1% power=0.25 resistance=220 package=THT]
  LED1 = smd LED [color="Green (555nm)" current=30mA package="0805 [SMD]"]

nets:
  N1: Part1.D13/SCK, LED1.anode
  N2: Part1.GND, R1.Pin_1
  N3: R1.Pin_0, LED1.cathode
