# Fritzing sketch fritzing_schematic (saved by Fritzing 0.9.10b)
breadboards: 1

parts:
  Part1 = Arduino Uno (Rev3)
  LED1 = LED - 5mm [color="Green (555nm)" current=0.030 package="5 mm [THT]"]
  S1 = Pushbutton [package="[THT]"]
  R1 = Resistor [tolerance=±1% power=0.25 resistance=220 package=THT]

nets:
  N1: Part1.D13/SCK, LED1.anode
  N2: Part1.D2, Part1.GND, S1.Pin_1, S1.Pin_2, R1.Pin_0
  N3: LED1.cathode, R1.Pin_1
  N4: S1.Pin_3, S1.Pin_4
